# Fritzing sketch 23LC1024-time-interval (saved by Fritzing 0.9.3b)
breadboards: 1

parts:
  Part1 = Arduino Mega 2560 (Rev3)
  23LCV1 = 23LCV1024 [part_number=23LCV1024 package="DIP (Dual Inline) [THT]"]

nets (from the breadboard view):
  N1: Part1.A8, Part1.D9_PWM, 23LCV1.VCC
  N2: Part1.D11_PWM, 23LCV1.VBAT
  N3: Part1.D10_PWM, 23LCV1.CS_
  N4: Part1.D50, Part1.GND, 23LCV1.SO/SIO1
  N5: Part1.D51, 23LCV1.SI/SIO0
  N6: Part1.D52, 23LCV1.SCK
