# Fritzing sketch 23LC1024-voltage (saved by Fritzing 0.9.3b)
breadboards: 1

parts:
  Part1 = Arduino Mega 2560 (Rev3)
  23LCV1 = 23LCV1024 [part_number=23LCV1024 package="DIP (Dual Inline) [THT]"]
  U4 = Mini-360 DC-DC Buck converter [package=THT]

nets (from the breadboard view):
  N1: Part1.A8, 23LCV1.VCC, U4.OUT+
  N2: Part1.D11_PWM, 23LCV1.VBAT
  N3: Part1.D10_PWM, 23LCV1.CS_
  N4: Part1.D9_PWM, U4.IN+
  N5: Part1.GND, U4.IN-
  N6: Part1.D50, 23LCV1.SO/SIO1
  N7: Part1.D51, 23LCV1.SI/SIO0
  N8: Part1.D52, 23LCV1.SCK
  N9: 23LCV1.NC, 23LCV1.VSS, U4.OUT-

custom parts:
  Mini-360 DC-DC Buck converter: Mini-360 DC-DC Buck converter. Tiny buck step down voltage converter, input voltage 4.75 to 23V output 1 to 17V adjustable. Available from ebay and the like.
