# Fritzing sketch CY62256NLL-enrollment-microSD (saved by Fritzing 0.9.3b)
breadboards: 2

parts:
  Part1 = Arduino Mega 2560 (Rev3)
  SRAM_Chip = IC, DIP package, 28 pins [chip_label=CY62256N]
  microSD2 = MicroSD Breakout

nets:
  N1: Part1.A8, Part1.D9_PWM, SRAM_Chip.pin28
  GND: Part1.GND, SRAM_Chip.pin14, microSD2.GND
  N2: Part1.D13_PWM, SRAM_Chip.pin20
  N3: Part1.D12_PWM, SRAM_Chip.pin22
  N4: Part1.D11_PWM, SRAM_Chip.pin27
  5V: Part1.5V, microSD2.5V
  N5: Part1.D7_PWM, microSD2.CS
  N6: Part1.D22, SRAM_Chip.pin10
  N7: Part1.D23, SRAM_Chip.pin9
  N8: Part1.D24, SRAM_Chip.pin8
  N9: Part1.D25, SRAM_Chip.pin7
  N10: Part1.D26, SRAM_Chip.pin6
  N11: Part1.D27, SRAM_Chip.pin5
  N12: Part1.D28, SRAM_Chip.pin4
  N13: Part1.D29, SRAM_Chip.pin3
  N14: Part1.D31, SRAM_Chip.pin1
  N15: Part1.D32, SRAM_Chip.pin26
  N16: Part1.D33, SRAM_Chip.pin2
  N17: Part1.D34, SRAM_Chip.pin23
  N18: Part1.D35, SRAM_Chip.pin21
  N19: Part1.D36, SRAM_Chip.pin24
  N20: Part1.D37, SRAM_Chip.pin25
  N21: Part1.D42, SRAM_Chip.pin19
  N22: Part1.D43, SRAM_Chip.pin18
  N23: Part1.D44, SRAM_Chip.pin17
  N24: Part1.D45, SRAM_Chip.pin16
  N25: Part1.D46, SRAM_Chip.pin15
  N26: Part1.D47, SRAM_Chip.pin13
  N27: Part1.D48, SRAM_Chip.pin12
  N28: Part1.D49, SRAM_Chip.pin11
  N29: Part1.D50, microSD2.DI
  N30: Part1.D51, microSD2.DO
  N31: Part1.D52, microSD2.CLK

custom parts:
  MicroSD Breakout: 5V-ready microSD Breakout with Level Shifter
