# Fritzing sketch CY62256NLL-time-interval (saved by Fritzing 0.9.3b)
breadboards: 1

parts:
  Part1 = Arduino Mega 2560 (Rev3)
  SRAM_Chip = IC, DIP package, 28 pins [chip_label=CY62256N]

nets:
  N1: Part1.A8, SRAM_Chip.pin28
  N2: Part1.D22, SRAM_Chip.pin10
  N3: Part1.D23, SRAM_Chip.pin9
  N4: Part1.D24, SRAM_Chip.pin8
  N5: Part1.D25, SRAM_Chip.pin7
  N6: Part1.D26, SRAM_Chip.pin6
  N7: Part1.D27, SRAM_Chip.pin5
  N8: Part1.D28, SRAM_Chip.pin4
  N9: Part1.D29, SRAM_Chip.pin3
  N10: Part1.D31, SRAM_Chip.pin1
  N11: Part1.D32, SRAM_Chip.pin26
  N12: Part1.D33, SRAM_Chip.pin2
  N13: Part1.D34, SRAM_Chip.pin23
  N14: Part1.D35, SRAM_Chip.pin21
  N15: Part1.D36, SRAM_Chip.pin24
  N16: Part1.D37, SRAM_Chip.pin25
  N17: Part1.D42, SRAM_Chip.pin19
  N18: Part1.D43, SRAM_Chip.pin18
  N19: Part1.D44, SRAM_Chip.pin17
  N20: Part1.D45, SRAM_Chip.pin16
  N21: Part1.D46, SRAM_Chip.pin15
  N22: Part1.D47, SRAM_Chip.pin13
  N23: Part1.D48, SRAM_Chip.pin12
  N24: Part1.D49, SRAM_Chip.pin11
  N25: Part1.D51, SRAM_Chip.pin20
  N26: Part1.D52, SRAM_Chip.pin22
  N27: Part1.D53, SRAM_Chip.pin27
  N28: Part1.GND, SRAM_Chip.pin14

notes:
  Black - GND
  Red - +5V
  Blue - Address Bus
  Green - Data Bus
